// Logisim project problem1.circ as structural Verilog: 1 circuit, main circuit main
module main (
  output [31:0] out_1,
  output [31:0] out_2
);

  wire clock_1_out, comparator_1_eq, comparator_2_eq, multiplexer_1_out;
  wire [4:0] adder_1_out, incrementer_1_p1, incrementer_1_p2, registerfile_1_p5, subtractor_1_out;
  wire [31:0] adder_2_out, multiplexer_2_out;

  Clock clock_1 (.out(clock_1_out));
  Comparator #(.width(5)) comparator_1 (.a(5'b10101), .b(adder_1_out), .eq(comparator_1_eq));  // open: gt, lt
  Multiplexer #(.enable("false")) multiplexer_1 (
    .in0(clock_1_out), .in1(1'b0), .out(multiplexer_1_out), .sel(comparator_1_eq));
  // Incrementer #(.width(5)) incrementer_1: pin names not known; wires that end beside it: incrementer_1_p1, incrementer_1_p2
  Comparator #(.width(5)) comparator_2 (.a(5'b00001), .b(adder_1_out), .eq(comparator_2_eq));  // open: gt, lt
  Register #(.width(5)) register_1 (
    .D(incrementer_1_p2), .en(1'b1), .clk(multiplexer_1_out), .Q(incrementer_1_p1));  // open: clr
  Multiplexer #(.width(32), .enable("false")) multiplexer_2 (
    .in0(adder_2_out), .in1(32'h1), .out(multiplexer_2_out), .sel(comparator_2_eq));
  Adder #(.width(5)) adder_1 (.a(incrementer_1_p1), .b(5'b00001), .out(adder_1_out));  // open: cin, cout
  Subtractor #(.width(5)) subtractor_1 (.a(adder_1_out), .b(5'b00001), .out(subtractor_1_out));  // open: bin, bout
  // RegisterFile registerfile_1: pin names not known; wires that end beside it: multiplexer_2_out, multiplexer_1_out, adder_1_out, subtractor_1_out, registerfile_1_p5, out_1, out_2
  Subtractor #(.width(5)) subtractor_2 (
    .a(subtractor_1_out), .b(5'b00001), .out(registerfile_1_p5));  // open: bin, bout
  Adder #(.width(32)) adder_2 (.a(out_1), .b(out_2), .out(adder_2_out));  // open: cin, cout
endmodule
