// Logisim project problem2.circ as structural Verilog: 1 circuit, main circuit main
module main (
);

  wire clock_1_out, comparator_1_eq, comparator_2_gt, multiplexer_1_out;
  wire [4:0] bit_extender_1_out;
  wire [31:0] adder_1_out, adder_2_out, multiplier_1_out, register_1_q, register_2_q, register_3_q,
       register_4_q, register_5_q;

  Clock clock_1 (.out(clock_1_out));
  Comparator #(.width(32)) comparator_1 (.a(register_1_q), .b(32'h18), .eq(comparator_1_eq));  // open: gt, lt
  Register #(.width(32)) register_1 (
    .D(adder_1_out), .en(1'b1), .clk(multiplexer_1_out), .Q(register_1_q));  // open: clr
  Adder #(.width(32)) adder_1 (.a(register_1_q), .b(32'h1), .out(adder_1_out));  // open: cin, cout
  Multiplexer #(.enable("false")) multiplexer_1 (
    .in0(clock_1_out), .in1(1'b0), .out(multiplexer_1_out), .sel(comparator_1_eq));
  Register #(.width(32)) register_2 (
    .D(register_1_q), .en(1'b1), .clk(multiplexer_1_out), .Q(register_2_q));  // open: clr
  Adder #(.width(32)) adder_2 (.a(register_2_q), .b(32'h1), .out(adder_2_out));  // open: cin, cout
  Register #(.width(32)) register_3 (
    .D(adder_2_out), .en(1'b1), .clk(multiplexer_1_out), .Q(register_3_q));  // open: clr
  Multiplier #(.width(32)) multiplier_1 (.a(register_3_q), .b(32'h5), .out(multiplier_1_out));  // open: cin, cout
  Register #(.width(32)) register_4 (
    .D(register_3_q), .en(1'b1), .clk(multiplexer_1_out), .Q(register_4_q));  // open: clr
  Register #(.width(32)) register_5 (
    .D(multiplier_1_out), .en(1'b1), .clk(multiplexer_1_out), .Q(register_5_q));  // open: clr
  Comparator #(.width(32)) comparator_2 (.a(register_1_q), .b(32'h2), .gt(comparator_2_gt));  // open: eq, lt
  Bit_Extender #(.in_width(32), .out_width(5)) bit_extender_1 (.in(register_4_q), .out(bit_extender_1_out));
  // RegisterFile registerfile_1: pin names not known; wires that end beside it: register_5_q, multiplexer_1_out, comparator_2_gt, bit_extender_1_out
endmodule
