// Logisim project mips-add.circ as structural Verilog
module main (
  input  in_1,
  input  ON_OFF,
  output [31:0] out_3,
  output [5:0] out_4,
  output [31:0] PCCounter
);

  wire clock_1_out, multiplexer_1_out, registerfile_1_p1, registerfile_1_p7;
  wire [4:0] multiplexer_3_out;
  wire [6:0] rom_1_data;
  wire [31:0] adder_1_out, bit_extender_1_out, multiplexer_2_out, multiplexer_4_out, registerfile_1_p8;

  Clock clock_1 (.out(clock_1_out));
  ROM #(.addrWidth(6), .dataWidth(7)) rom_1 (.addr(out_3[31:26]), .data(rom_1_data));
  Multiplexer #(.enable("false")) multiplexer_1 (.in0(in_1), .in1(clock_1_out), .out(multiplexer_1_out), .sel(ON_OFF));
  Multiplexer #(.width(32), .enable("false")) multiplexer_2 (
    .in0({32{1'b0}}), .in1(adder_1_out), .out(multiplexer_2_out), .sel(ON_OFF));
  PC pc_1 (.NewBits(multiplexer_2_out), .clk(multiplexer_1_out), .CurrentBits(PCCounter));
  Adder #(.width(32)) adder_1 (.a(32'h4), .b(PCCounter), .out(adder_1_out));  // open: cin, cout
  // MIPSProgramROM mipsprogramrom_1: pin names not known; wires that end beside it: PCCounter
  assign bit_extender_1_out = {{16{out_3[15]}}, out_3[15:0]};  // Bit_Extender bit_extender_1
  Multiplexer #(.width(5), .enable("false")) multiplexer_3 (
    .in0(out_3[15:11]), .in1(out_3[20:16]), .out(multiplexer_3_out), .sel(rom_1_data[1]));
  // RegisterFile registerfile_1: pin names not known; wires that end beside it: registerfile_1_p1, multiplexer_1_out, rom_1_data[0], multiplexer_3_out, out_3[25:21], out_3[20:16], registerfile_1_p7, registerfile_1_p8
  Multiplexer #(.width(32), .enable("false")) multiplexer_4 (
    .in0(registerfile_1_p8), .in1(bit_extender_1_out), .out(multiplexer_4_out), .sel(rom_1_data[2]));
  // Mips_ALU mips_alu_1: pin names not known; wires that end beside it: registerfile_1_p7, multiplexer_4_out, rom_1_data[6:3], registerfile_1_p1

  assign out_4 = out_3[31:26];

  // Notes on the sheet:
  //   contents of rom_1 (hex, n*v repeats v):
  //   11 7*0 17 17
  //   contents of mipsprogramrom_1 (hex, n*v repeats v):
  //   addiu $s1, $zero, 2 addu $s2, $s0, $s1
endmodule

module Remember1bit (
  input  NewBit,
  input  clk,
  output CurrentBit
);

  wire xor_1_out;

  xor xor_1 (xor_1_out, CurrentBit, NewBit);
  T_Flip_Flop t_ff_1 (.T(xor_1_out), .clk(clk), .Qn(CurrentBit));  // open: Q, reset, preset

  // Notes on the sheet:
  //   CurrentBit: pull=down
endmodule

module Remember4bit (
  input  [7:0] NewBits,
  input  clk,
  output [7:0] CurrentBit
);

  Remember1bit remember1bit_1 (.NewBit(NewBits[0]), .clk(clk), .CurrentBit(CurrentBit[0]));
  Remember1bit remember1bit_2 (.NewBit(NewBits[1]), .clk(clk), .CurrentBit(CurrentBit[1]));
  Remember1bit remember1bit_3 (.NewBit(NewBits[2]), .clk(clk), .CurrentBit(CurrentBit[2]));
  Remember1bit remember1bit_4 (.NewBit(NewBits[3]), .clk(clk), .CurrentBit(CurrentBit[3]));
  Remember1bit remember1bit_5 (.NewBit(NewBits[4]), .clk(clk), .CurrentBit(CurrentBit[4]));
  Remember1bit remember1bit_6 (.NewBit(NewBits[5]), .clk(clk), .CurrentBit(CurrentBit[5]));
  Remember1bit remember1bit_7 (.NewBit(NewBits[6]), .clk(clk), .CurrentBit(CurrentBit[6]));
  Remember1bit remember1bit_8 (.NewBit(NewBits[7]), .clk(clk), .CurrentBit(CurrentBit[7]));

  // Notes on the sheet:
  //   clk: pull=up
  //   NewBits: pull=down
endmodule

module PC (
  input  [31:0] NewBits,
  input  clk,
  output [31:0] CurrentBits
);

  Remember4bit remember4bit_1 (.NewBits(NewBits[7:0]), .clk(clk), .CurrentBit(CurrentBits[7:0]));
  Remember4bit remember4bit_2 (.NewBits(NewBits[15:8]), .clk(clk), .CurrentBit(CurrentBits[15:8]));
  Remember4bit remember4bit_3 (.NewBits(NewBits[23:16]), .clk(clk), .CurrentBit(CurrentBits[23:16]));
  Remember4bit remember4bit_4 (.NewBits(NewBits[31:24]), .clk(clk), .CurrentBit(CurrentBits[31:24]));
endmodule

module StartSelect (
);

  Multiplexer #(.enable("false")) multiplexer_1 ();  // open: in0, in1, out, sel
endmodule
