// Logisim project mips-single.circ as structural Verilog
module main (
  input  ON_OFF,
  output [5:0] op_code,
  output [31:0] out_3,
  output [5:0] func,
  output [3:0] out_5,
  output [5:0] func_2,
  output [31:0] out_7,
  output [31:0] out_8,
  output [31:0] out_9,
  output [31:0] out_10,
  output [31:0] out_11,
  output [5:0] opcode
);

  wire clock_1_out, comparator_2_eq, multiplexer_1_out, multiplexer_9_out, not_1_out, not_2_out, not_3_out,
       not_4_out, not_5_out, or_1_out;
  wire [0:0] comparator_1_lt;
  wire [4:0] multiplexer_7_out, multiplexer_8_out;
  wire [12:0] multiplexer_5_out, rom_1_data, rom_2_data;
  wire [23:0] bit_extender_3_out;
  wire [27:0] bit_extender_1_out, shifter_2_out;
  wire [31:0] adder_1_out, adder_2_out, bit_extender_2_out, mips_alu_1_p5, multiplexer_3_out,
       multiplexer_4_out, multiplexer_6_out, multiplexer_11_out, multiplexer_12_out, multiplexer_13_out,
       pc_1_currentbits, registerfile_1_p8, shifter_1_out;

  Clock clock_1 (.out(clock_1_out));
  ROM #(.addrWidth(6), .dataWidth(13)) rom_1 (.addr(func_2), .data(rom_1_data));
  ROM #(.addrWidth(6), .dataWidth(13)) rom_2 (.addr(func), .data(rom_2_data));
  Multiplexer #(.enable("false")) multiplexer_1 (.in0(1'b0), .in1(clock_1_out), .out(multiplexer_1_out), .sel(ON_OFF));
  Multiplexer #(.width(32), .enable("false")) multiplexer_2 (
    .in0(multiplexer_3_out), .in1(multiplexer_6_out), .out(out_10), .sel(multiplexer_5_out[3]));
  PC pc_1 (.NewBits(out_10), .clk(multiplexer_1_out), .CurrentBits(pc_1_currentbits));
  not not_1 (not_1_out, ON_OFF);
  Multiplexer #(.width(32), .enable("false")) multiplexer_3 (
    .in0(adder_2_out), .in1(adder_1_out), .out(multiplexer_3_out), .sel(not_3_out));
  Multiplexer #(.width(32), .enable("false")) multiplexer_4 (
    .in0(pc_1_currentbits), .in1({32{1'b0}}), .out(multiplexer_4_out), .sel(not_1_out));
  Multiplexer #(.width(13), .enable("false")) multiplexer_5 (
    .in0(rom_1_data), .in1(rom_2_data), .out({multiplexer_5_out[12:11], out_5, multiplexer_5_out[6:0]}),
    .sel(not_2_out));
  not not_2 (not_2_out, or_1_out);
  or or_1 (or_1_out, func_2[0], func_2[1], func_2[2], func_2[3], func_2[4], func_2[5]);
  Adder #(.width(32)) adder_1 (.a(32'h4), .b(multiplexer_4_out), .out(adder_1_out));  // open: cin, cout
  Multiplexer #(.width(32), .enable("false")) multiplexer_6 (
    .in0({multiplexer_4_out[31:28], shifter_2_out}), .in1(registerfile_1_p8), .out(multiplexer_6_out),
    .sel(multiplexer_5_out[1]));
  Shifter #(.width(32)) shifter_1 (.in(bit_extender_2_out), .\dist (5'b00010), .out(shifter_1_out));
  Adder #(.width(32)) adder_2 (.a(shifter_1_out), .b(adder_1_out), .out(adder_2_out));  // open: cin, cout
  not not_3 (not_3_out, multiplexer_9_out);
  // MIPSProgramROM mipsprogramrom_1: pin names not known; wires that end beside it: multiplexer_4_out, {func_2, out_11[25:6], func}
  assign bit_extender_1_out = {{2{out_11[25]}}, {out_11[25:6], func}};  // Bit_Extender bit_extender_1
  Multiplexer #(.width(5), .enable("false")) multiplexer_7 (
    .in0(multiplexer_8_out), .in1({5{1'b1}}), .out(multiplexer_7_out), .sel(multiplexer_5_out[2]));
  assign bit_extender_2_out = {{16{out_11[15]}}, {out_11[15:6], func}};  // Bit_Extender bit_extender_2
  Multiplexer #(.width(5), .enable("false")) multiplexer_8 (
    .in0(out_11[15:11]), .in1(out_11[20:16]), .out(multiplexer_8_out), .sel(multiplexer_5_out[11]));
  Shifter #(.width(28)) shifter_2 (.in(bit_extender_1_out), .\dist (5'b00010), .out(shifter_2_out));
  Multiplexer #(.enable("false")) multiplexer_9 (
    .in0(1'b0), .in1(comparator_2_eq), .out(multiplexer_9_out), .sel(multiplexer_5_out[0]));
  Multiplexer #(.width(32), .enable("false")) multiplexer_10 (
    .in0(multiplexer_12_out), .in1(adder_1_out), .out(out_3), .sel(multiplexer_5_out[2]));
  // RegisterFile registerfile_1: pin names not known; wires that end beside it: out_3, multiplexer_1_out, multiplexer_5_out[12], multiplexer_7_out, multiplexer_9_out, out_11[25:21], out_11[20:16], registerfile_1_p8, out_8
  Multiplexer #(.width(32), .enable("false")) multiplexer_11 (
    .in0(out_8), .in1(bit_extender_2_out), .out(multiplexer_11_out), .sel(multiplexer_5_out[11]));
  Multiplexer #(.width(32), .enable("false")) multiplexer_12 (
    .in0(out_7), .in1(multiplexer_13_out), .out(multiplexer_12_out), .sel(not_4_out));
  not not_4 (not_4_out, multiplexer_5_out[5]);
  Comparator #(.width(32)) comparator_1 (
    .a(registerfile_1_p8), .b(multiplexer_11_out), .lt(comparator_1_lt[0]));  // open: gt, eq
  // Mips_ALU mips_alu_1: pin names not known; wires that end beside it: registerfile_1_p8, multiplexer_11_out, out_5, out_11[10:6], mips_alu_1_p5
  Comparator #(.width(32)) comparator_2 (.a(multiplexer_13_out), .b(32'h1), .eq(comparator_2_eq));  // open: gt, lt
  Multiplexer #(.width(32), .enable("false")) multiplexer_13 (
    .in0(mips_alu_1_p5), .in1({{31{1'b0}}, comparator_1_lt[0]}), .out(multiplexer_13_out),
    .sel(multiplexer_5_out[4]));
  Bit_Extender #(.in_width(32), .out_width(24)) bit_extender_3 (.in(multiplexer_13_out), .out(bit_extender_3_out));
  not not_5 (not_5_out, ON_OFF);
  // MIPS_RAM #(.addrWidth(24)) mips_ram_1: pin names not known; wires that end beside it: bit_extender_3_out, out_8, multiplexer_5_out[6], 4'b1111, multiplexer_1_out, multiplexer_5_out[5], not_5_out, out_7

  assign op_code = func_2;
  assign opcode = func_2;
  assign out_9 = out_8;
  assign {out_11[31:26], out_11[5:0]} = {func_2, func};

  // Notes on the sheet:
  //   contents of rom_1 (hex, n*v repeats v):
  //   0 0 8 100c 581 481 0 0 0 1900 1810 1810 1c00 1d00 1e00 20*0 1920 7*0 940
  //   contents of rom_2 (hex, n*v repeats v):
  //   1000 0 1200 1280 4*0 a 24*0 1100 0 1300 1400 1500 1600 1700 0 0 1010 1010
  //   contents of mipsprogramrom_1 (hex, n*v repeats v):
  //   #init   addu $sp, $zero, $zero  addu $ra, $zero, $zero          addiu $sp, $sp, -4 #for n argument
  //   #you can change this line to whatever you want  addiu $t0, $zero, 7     sw $t0, 0($sp)          jal
  //   HAILSTONE   j EXIT # hailstone(int n) need one argument HAILSTONE:  addiu $sp, $sp, -8      sw $ra,
  //   4($sp) #store add address of$ra         sw $fp, 0($sp) #store address of $fp    addu $fp, $sp, $zero
  //   lw $s0, 8($fp) #load argument n         addiu $s1, $zero, 1 # 1         #if n==1 return 0       beq
  //   $s0, $s1, RETURN_ZERO       #n%2 = n&(2-1) = n&1    andi $s2, $s0, 1        #if (n%2) == 0  beq $s2,
  //   $zero, RETURN_L1       #else RETURN_L2:        #load next function     #we need to assign new n/2
  //   addiu $sp, $sp, -4      #we know $s0 is n and we need to make n+1       addu $s4, $s0, $s0 #n*2
  //   addu $s4, $s4, $s0 #n*2+n = 3*n         addiu $s4, $s4, 1 #n+1  sw $s4, 0($sp) #store augment   jal
  //   HAILSTONE #recursive        #when it out    #we don't need n anymore and don't need to load for use
  //   addiu $sp, $sp, 4       lw $ra, 4($sp)  lw $fp, 0($sp)          addiu $sp, $sp, 8       addiu $a0,
  //   $a0, 1 #return 1+recusive    jr $ra RETURN_ZERO:     lw $ra, 4($sp)  lw $fp, 0($sp)  addiu $sp, $sp,
  //   8       #we will use a0 to return this function         addiu $a0, $a0, 0 #return 0     jr $ra
  //   RETURN_L1:      #load next function     #we need to assign new n/2      addiu $sp, $sp, -4      #we
  //   know $s0 is n and we need to make n/2 use SRA       sra $s3, $s0, 1 #n/2    sw $s3, 0($sp) #store
  //   augment   jal HAILSTONE #recursive        #when it out    #we don't need n anymore and don't need to
  //   load for use         addiu $sp, $sp, 4       lw $ra, 4($sp)  lw $fp, 0($sp)          addiu $sp, $sp,
  //   8       addiu $a0, $a0, 1 #return 1+recursive   jr $ra EXIT:    #just exit we must use syscall  #but
  //   it can't   #we will just move a0 to t0     addu $t0, $a0, $zero
endmodule

module Remember1bit (
  input  NewBit,
  input  clk,
  output CurrentBit
);

  wire xor_1_out;

  xor xor_1 (xor_1_out, CurrentBit, NewBit);
  T_Flip_Flop t_ff_1 (.T(xor_1_out), .clk(clk), .Qn(CurrentBit));  // open: Q, reset, preset

  // Notes on the sheet:
  //   CurrentBit: pull=down
endmodule

module Remember4bit (
  input  [7:0] NewBits,
  input  clk,
  output [7:0] CurrentBit
);

  Remember1bit remember1bit_1 (.NewBit(NewBits[0]), .clk(clk), .CurrentBit(CurrentBit[0]));
  Remember1bit remember1bit_2 (.NewBit(NewBits[1]), .clk(clk), .CurrentBit(CurrentBit[1]));
  Remember1bit remember1bit_3 (.NewBit(NewBits[2]), .clk(clk), .CurrentBit(CurrentBit[2]));
  Remember1bit remember1bit_4 (.NewBit(NewBits[3]), .clk(clk), .CurrentBit(CurrentBit[3]));
  Remember1bit remember1bit_5 (.NewBit(NewBits[4]), .clk(clk), .CurrentBit(CurrentBit[4]));
  Remember1bit remember1bit_6 (.NewBit(NewBits[5]), .clk(clk), .CurrentBit(CurrentBit[5]));
  Remember1bit remember1bit_7 (.NewBit(NewBits[6]), .clk(clk), .CurrentBit(CurrentBit[6]));
  Remember1bit remember1bit_8 (.NewBit(NewBits[7]), .clk(clk), .CurrentBit(CurrentBit[7]));

  // Notes on the sheet:
  //   clk: pull=up
  //   NewBits: pull=down
endmodule

module PC (
  input  [31:0] NewBits,
  input  clk,
  output [31:0] CurrentBits
);

  Remember4bit remember4bit_1 (.NewBits(NewBits[7:0]), .clk(clk), .CurrentBit(CurrentBits[7:0]));
  Remember4bit remember4bit_2 (.NewBits(NewBits[15:8]), .clk(clk), .CurrentBit(CurrentBits[15:8]));
  Remember4bit remember4bit_3 (.NewBits(NewBits[23:16]), .clk(clk), .CurrentBit(CurrentBits[23:16]));
  Remember4bit remember4bit_4 (.NewBits(NewBits[31:24]), .clk(clk), .CurrentBit(CurrentBits[31:24]));
endmodule

module StartSelect (
);

  Multiplexer #(.enable("false")) multiplexer_1 ();  // open: in0, in1, out, sel
endmodule
