// Logisim project mips_pipeline.circ as structural Verilog: 12 circuits, main circuit main
module main (
  output out_1,
  output out_2,
  output out_3,
  output [31:0] out_4,
  output [31:0] out_5,
  output [31:0] out_6,
  output [31:0] out_7,
  output [19:0] out_8,
  output [31:0] out_9,
  output [31:0] out_10,
  output [31:0] out_11,
  output out_12,
  output [4:0] out_13,
  output [31:0] out_14,
  output [31:0] out_15,
  output [31:0] out_16,
  output [31:0] out_17,
  output [31:0] out_18,
  output [31:0] out_19,
  output [31:0] out_20,
  output [31:0] out_21
);

  wire clock_1_out, controlregister_1_is_branch, controlregister_1_is_imediate, controlregister_1_is_jump,
       controlregister_1_is_jump_register_save, controlregister_1_is_junp_register,
       controlregister_1_is_write_register, controlregister_1_load, controlregister_1_set_less,
       controlregister_1_store, controlregister_2_is_imediate, controlregister_2_is_write_register,
       controlregister_2_load, controlregister_2_store, controlregister_3_is_imediate,
       controlregister_3_is_write_register, controlregister_3_load, controlunit_1_branch,
       controlunit_1_isimediate, controlunit_1_isjump, controlunit_1_isjumpregister,
       controlunit_1_isjumpregistersave, controlunit_1_load, controlunit_1_setless, controlunit_1_store,
       controlunit_1_writeregister, exepart_1_isbranch, not_1_out, or_1_out;
  wire [3:0] controlregister_1_aluopt, controlunit_1_aluopt;
  wire [4:0] id_exe_1_sa, multiplexer_2_out, multiplexer_3_out;
  wire [31:0] bit_extender_1_out, exe_mem_1_op, exe_mem_1_sw_value, exe_mem_1_value, id_exe_1_next_line,
       id_exe_1_sw_value, if_id_1_next_line, ifpart_1_next_line, ifpart_1_op, mem_wb_1_alu_value,
       mem_wb_1_mem_value, multiplexer_1_out;

  Clock clock_1 (.out(clock_1_out));
  IFPart ifpart_1 (
    .jump(controlregister_1_is_jump), .next_line(ifpart_1_next_line), .op(ifpart_1_op), .clock(clock_1_out),
    .jump_value(out_4), .branch(exepart_1_isbranch), .enable(1'b1), .in_op(out_7),
    .is_next_line(id_exe_1_next_line), .will_branch(controlregister_1_is_branch),
    .current_line_number(out_19), .is_jump_register(controlregister_1_is_junp_register));
  IF_ID if_id_1 (
    .next_line(if_id_1_next_line), .op(out_9), .in_op(ifpart_1_op), .clock(clock_1_out),
    .in_next_line(ifpart_1_next_line), .WE(1'b1));
  ControlUnit controlunit_1 (
    .SetLess(controlunit_1_setless), .isJumpRegisterSave(controlunit_1_isjumpregistersave),
    .branch(controlunit_1_branch), .store(controlunit_1_store), .ALUopt(controlunit_1_aluopt),
    .isJumpRegister(controlunit_1_isjumpregister), .isJump(controlunit_1_isjump), .load(controlunit_1_load),
    .isImediate(controlunit_1_isimediate), .writeRegister(controlunit_1_writeregister), .instruction(out_9));
  or or_1 (or_1_out, controlregister_3_is_write_register, controlregister_1_is_jump_register_save);
  Multiplexer #(.width(32), .enable("false")) multiplexer_1 (
    .in0(out_10), .in1(id_exe_1_next_line), .out(multiplexer_1_out),
    .sel(controlregister_1_is_jump_register_save));
  Multiplexer #(.width(5), .enable("false")) multiplexer_2 (
    .in0(multiplexer_3_out), .in1({5{1'b1}}), .out(multiplexer_2_out),
    .sel(controlregister_1_is_jump_register_save));
  Multiplexer #(.width(5), .enable("false")) multiplexer_3 (
    .in0(out_16[15:11]), .in1(out_16[20:16]), .out(multiplexer_3_out), .sel(controlregister_3_is_imediate));
  // RegisterFile registerfile_1: pin names not known; wires that end beside it: multiplexer_1_out, clock_1_out, or_1_out, multiplexer_2_out, out_9[25:21], out_9[20:16], out_5, out_6
  assign bit_extender_1_out = {{16{out_9[15]}}, out_9[15:0]};  // Bit_Extender bit_extender_1
  Multiplexer #(.width(32), .enable("false")) multiplexer_4 (
    .in0(out_6), .in1(bit_extender_1_out), .out(out_14), .sel(controlunit_1_isimediate));
  ID_EXE id_exe_1 (
    .in_op(out_9), .in_A(out_5), .in_B(out_14), .in_SA(out_9[10:6]), .is_next_line(if_id_1_next_line),
    .in_sw_value(out_6), .clock(clock_1_out), .WE(1'b1), .op(out_7), .A(out_4), .B(out_21), .SA(id_exe_1_sa),
    .next_line(id_exe_1_next_line), .sw_value(id_exe_1_sw_value));
  ControlRegister controlregister_1 (
    .is_jump(controlregister_1_is_jump), .is_jump_register_save(controlregister_1_is_jump_register_save),
    .is_junp_register(controlregister_1_is_junp_register), .is_branch(controlregister_1_is_branch),
    .clock(clock_1_out), .WE(1'b1), .in_is_write_register(controlunit_1_writeregister),
    .in_is_imediate(controlunit_1_isimediate), .in_ALUopt(controlunit_1_aluopt),
    .in_store(controlunit_1_store), .in_load(controlunit_1_load), .in_set_less(controlunit_1_setless),
    .in_is_jump(controlunit_1_isjump), .in_is_jump_register_save(controlunit_1_isjumpregistersave),
    .in_is_jump_register(controlunit_1_isjumpregister), .in_is_branch(controlunit_1_branch),
    .set_less(controlregister_1_set_less), .load(controlregister_1_load), .store(controlregister_1_store),
    .ALUopt(controlregister_1_aluopt), .is_imediate(controlregister_1_is_imediate),
    .is_write_register(controlregister_1_is_write_register));
  EXEPart exepart_1 (
    .ALU_Op(controlregister_1_aluopt), .A(out_4), .isSetLess(controlregister_1_set_less),
    .isBranch(exepart_1_isbranch), .SA(id_exe_1_sa), .B(out_21), .value(out_15));
  EXE_MEM exe_mem_1 (
    .in_op(out_7), .in_value(out_15), .in_sw_value(id_exe_1_sw_value), .WE(1'b1), .clock(clock_1_out),
    .op(exe_mem_1_op), .value(exe_mem_1_value), .sw_value(exe_mem_1_sw_value));  // open: in_B, in_next_line, B, next_line
  ControlRegister controlregister_2 (
    .clock(clock_1_out), .WE(1'b1), .in_is_write_register(controlregister_1_is_write_register),
    .in_is_imediate(controlregister_1_is_imediate), .in_store(controlregister_1_store),
    .in_load(controlregister_1_load), .load(controlregister_2_load), .store(controlregister_2_store),
    .is_imediate(controlregister_2_is_imediate), .is_write_register(controlregister_2_is_write_register));  // open: is_jump, is_jump_register_save, is_junp_register, is_branch, in_ALUopt, in_set_less, in_is_jump, in_is_jump_register_save, in_is_jump_register, in_is_branch, set_less, ALUopt
  Bit_Extender #(.in_width(32), .out_width(20)) bit_extender_2 (.in(exe_mem_1_value), .out(out_8));
  not not_1 (not_1_out, 1'b1);
  // MIPS_RAM mips_ram_1: pin names not known; wires that end beside it: out_8, exe_mem_1_sw_value, controlregister_2_store, 4'b1111, clock_1_out, controlregister_2_load, not_1_out, out_17
  MEM_WB mem_wb_1 (
    .in_op(exe_mem_1_op), .in_mem_value(out_17), .in_ALU_value(exe_mem_1_value), .clock(clock_1_out),
    .WE(1'b1), .op(out_16), .mem_value(mem_wb_1_mem_value), .ALU_value(mem_wb_1_alu_value));
  ControlRegister controlregister_3 (
    .clock(clock_1_out), .WE(1'b1), .in_is_write_register(controlregister_2_is_write_register),
    .in_is_imediate(controlregister_2_is_imediate), .in_load(controlregister_2_load),
    .load(controlregister_3_load), .is_imediate(controlregister_3_is_imediate),
    .is_write_register(controlregister_3_is_write_register));  // open: is_jump, is_jump_register_save, is_junp_register, is_branch, in_ALUopt, in_store, in_set_less, in_is_jump, in_is_jump_register_save, in_is_jump_register, in_is_branch, set_less, store, ALUopt
  WBPart wbpart_1 (
    .load(controlregister_3_load), .ALU_value(mem_wb_1_alu_value), .Mem_value(mem_wb_1_mem_value),
    .WriteValue(out_10));

  assign out_11 = out_7;
  assign out_13 = out_9[20:16];
  assign out_20 = out_4;

  // Notes on the sheet:
  //   op
  //   A
  //   B
  //   value
endmodule

module IFPart (
  input  [31:0] in_op,
  input  [31:0] jump_value,
  input  [31:0] is_next_line,
  input  is_jump_register,
  input  jump,
  input  branch,
  input  will_branch,
  input  enable,
  input  clock,
  output [31:0] op,
  output [31:0] next_line,
  output [31:0] current_line_number
);

  wire and_1_out;
  wire [27:0] bit_extender_2_out, shifter_1_out;
  wire [31:0] adder_1_out, bit_extender_1_out, multiplexer_1_out, multiplexer_2_out, register_1_q,
       shifter_2_out;

  assign bit_extender_1_out = {{16{1'b0}}, in_op[15:0]};  // Bit_Extender bit_extender_1
  assign bit_extender_2_out = {{2{1'b0}}, in_op[25:0]};  // Bit_Extender bit_extender_2
  Shifter #(.width(28)) shifter_1 (.in(bit_extender_2_out), .\dist (5'b00010), .out(shifter_1_out));
  Shifter #(.width(32)) shifter_2 (.in(bit_extender_1_out), .\dist (5'b00010), .out(shifter_2_out));
  and and_1 (and_1_out, branch, will_branch);
  Multiplexer #(.width(32), .enable("false")) multiplexer_1 (
    .in0(next_line), .in1({is_next_line[31:28], shifter_1_out}), .out(multiplexer_1_out), .sel(jump));
  Adder #(.width(32)) adder_1 (.a(is_next_line), .b(shifter_2_out), .out(adder_1_out));  // open: cin, cout
  Multiplexer #(.width(32), .enable("false")) multiplexer_2 (
    .in0(multiplexer_1_out), .in1(adder_1_out), .out(multiplexer_2_out), .sel(and_1_out));
  Register #(.width(32)) register_1 (.D(current_line_number), .en(enable), .clk(clock), .Q(register_1_q));  // open: clr
  Adder #(.width(32)) adder_2 (.a(register_1_q), .b(32'h4), .out(next_line));  // open: cin, cout
  // MIPSProgramROM mipsprogramrom_1: pin names not known; wires that end beside it: register_1_q, op
  Multiplexer #(.width(32), .enable("false")) multiplexer_3 (
    .in0(multiplexer_2_out), .in1(jump_value), .out(current_line_number), .sel(is_jump_register));

  // Notes on the sheet:
  //   contents of mipsprogramrom_1 (hex, n*v repeats v):
  //   #init   addu $sp, $zero, $zero  addu $ra, $zero, $zero          addiu $sp, $sp, -4 #for n argument
  //   #you can change this line to whatever you want  addiu $t0, $zero, 7     nop     nop     nop     sw
  //   $t0, 0($sp)          jal HAILSTONE   nop     nop     j EXIT  nop     nop # hailstone(int n) need one
  //   argument HAILSTONE:     addiu $sp, $sp, -8      nop     nop     nop     sw $ra, 4($sp) #store add
  //   address of$ra         sw $fp, 0($sp) #store address of $fp    addu $fp, $sp, $zero    nop     nop
  //   nop     lw $s0, 8($fp) #load argument n         addiu $s1, $zero, 1 # 1         nop     nop     nop
  //   #if n==1 return 0       beq $s0, $s1, RETURN_ZERO       nop     nop     #n%2 = n&(2-1) = n&1    andi
  //   $s2, $s0, 1        nop     nop     nop     #if (n%2) == 0  beq $s2, $zero, RETURN_L1       #else
  //   nop     nop RETURN_L2:  #load next function     #we need to assign new n/2      addiu $sp, $sp, -4
  //   #we know $s0 is n and we need to make n+1       addu $s4, $s0, $s0 #n*2         nop     nop     nop
  //   addu $s4, $s4, $s0 #n*2+n = 3*n         nop     nop     nop     addiu $s4, $s4, 1 #n+1  nop     nop
  //   nop     sw $s4, 0($sp) #store augment   jal HAILSTONE #recursive        nop     nop     #when it out
  //   #we don't need n anymore and don't need to load for use         addiu $sp, $sp, 4       nop     nop
  //   nop     lw $ra, 4($sp)  lw $fp, 0($sp)          addiu $sp, $sp, 8       addiu $a0, $a0, 1 #return
  //   1+recusive    jr $ra  nop     nop RETURN_ZERO:        lw $ra, 4($sp)  lw $fp, 0($sp)  addiu $sp,
  //   $sp, 8       #we will use a0 to return this function         addiu $a0, $a0, 0 #return 0     jr $ra
  //   nop     nop  RETURN_L1:         #load next function     #we need to assign new n/2      addiu $sp,
  //   $sp, -4      #we know $s0 is n and we need to make n/2 use SRA       sra $s3, $s0, 1 #n/2    nop
  //   nop     nop     sw $s3, 0($sp) #store augment   jal HAILSTONE #recursive        nop     nop
  //   #when it out    #we don't need n anymore and don't need to load for use         addiu $sp, $sp, 4
  //   nop     nop     nop     lw $ra, 4($sp)  lw $fp, 0($sp)          addiu $sp, $sp, 8       addiu $a0,
  //   $a0, 1 #return 1+recursive   jr $ra  nop     nop EXIT:       #just exit we must use syscall  #but it
  //   can't   #we will just move a0 to t0     addu $t0, $a0, $zero
endmodule

module IDPart (
  input  [31:0] write_data,
  input  clock,
  input  is_write_register,
  input  is_jump_register_save,
  input  is_imediate,
  input  [31:0] old_op,
  input  [31:0] op,
  output [31:0] A,
  output [31:0] B,
  output [4:0] SA
);

  wire [4:0] multiplexer_1_out, multiplexer_2_out;
  wire [31:0] bit_extender_1_out, registerfile_1_p8;

  Multiplexer #(.width(5), .enable("false")) multiplexer_1 (
    .in0(multiplexer_2_out), .in1({5{1'b1}}), .out(multiplexer_1_out), .sel(is_jump_register_save));
  Multiplexer #(.width(5), .enable("false")) multiplexer_2 (
    .in0(old_op[15:11]), .in1(old_op[20:16]), .out(multiplexer_2_out), .sel(is_imediate));
  // RegisterFile registerfile_1: pin names not known; wires that end beside it: write_data, clock, is_write_register, multiplexer_1_out, op[25:21], op[20:16], A, registerfile_1_p8
  assign bit_extender_1_out = {{16{op[15]}}, op[15:0]};  // Bit_Extender bit_extender_1
  Multiplexer #(.width(32), .enable("false")) multiplexer_3 (
    .in0(registerfile_1_p8), .in1(bit_extender_1_out), .out(B), .sel(is_imediate));

  assign SA = op[10:6];
endmodule

module EXEPart (
  input  [31:0] A,
  input  [31:0] B,
  input  isSetLess,
  input  [3:0] ALU_Op,
  input  [4:0] SA,
  output isBranch,
  output [31:0] value
);

  wire comparator_1_lt;
  wire [31:0] bit_extender_1_out, mips_alu_1_p7;

  Comparator #(.width(32)) comparator_1 (.a(A), .b(B), .lt(comparator_1_lt));  // open: gt, eq
  // Mips_ALU mips_alu_1: pin names not known; wires that end beside it: B, A, A, B, ALU_Op, SA, mips_alu_1_p7
  assign bit_extender_1_out = {{31{1'b0}}, comparator_1_lt};  // Bit_Extender bit_extender_1
  Multiplexer #(.width(32), .enable("false")) multiplexer_1 (
    .in0(mips_alu_1_p7), .in1(bit_extender_1_out), .out(value), .sel(isSetLess));
  Comparator #(.width(32)) comparator_2 (.a(32'h1), .b(value), .eq(isBranch));  // open: gt, lt
endmodule

module MEMPart (
  input  [31:0] op,
  input  [31:0] data,
  input  store,
  input  clock,
  input  load,
  input  clear,
  output [31:0] value
);

  wire [19:0] bit_extender_1_out;

  Bit_Extender #(.in_width(32), .out_width(20), .\type ("zero")) bit_extender_1 (.in(op), .out(bit_extender_1_out));
  // MIPS_RAM mips_ram_1: pin names not known; wires that end beside it: bit_extender_1_out, data, store, 4'b1111, clock, load, clear, value
endmodule

module WBPart (
  input  load,
  input  [31:0] ALU_value,
  input  [31:0] Mem_value,
  output [31:0] WriteValue
);

  Multiplexer #(.width(32), .enable("false")) multiplexer_1 (
    .in0(ALU_value), .in1(Mem_value), .out(WriteValue), .sel(load));
endmodule

module ControlUnit (
  input  [31:0] instruction,
  output branch,
  output isJumpRegister,
  output isJumpRegisterSave,
  output isJump,
  output SetLess,
  output load,
  output store,
  output [3:0] ALUopt,
  output isImediate,
  output writeRegister
);

  wire comparator_1_eq;
  wire [12:0] funcRom_data, opRom_data;

  Comparator #(.width(6)) comparator_1 (.a({6{1'b0}}), .b(instruction[31:26]), .eq(comparator_1_eq));  // open: gt, lt
  ROM #(.addrWidth(6), .dataWidth(13)) opRom (.addr(instruction[31:26]), .data(opRom_data));
  ROM #(.addrWidth(6), .dataWidth(13)) funcRom (.addr(instruction[5:0]), .data(funcRom_data));
  Multiplexer #(.width(13), .enable("false")) multiplexer_1 (
    .in0(opRom_data), .in1(funcRom_data),
    .out({writeRegister, isImediate, ALUopt, store, load, SetLess, isJump, isJumpRegisterSave, isJumpRegister, branch}),
    .sel(comparator_1_eq));

  // Notes on the sheet:
  //   contents of opRom (hex, n*v repeats v):
  //   0 0 8 100c 581 481 0 0 0 1900 1810 1810 1c00 1d00 1e00 20*0 1920 7*0 940
  //   contents of funcRom (hex, n*v repeats v):
  //   1000 0 1200 1280 4*0 a 24*0 1100 0 1300 1400 1500 1600 1700 0 0 1010 1010
endmodule

module IF_ID (
  input  [31:0] in_op,
  input  [31:0] in_next_line,
  input  WE,
  input  clock,
  output [31:0] op,
  output [31:0] next_line
);

  Register #(.width(32)) register_1 (.D(in_op), .en(WE), .clk(clock), .Q(op));  // open: clr
  Register #(.width(32)) register_2 (.D(in_next_line), .en(WE), .clk(clock), .Q(next_line));  // open: clr
endmodule

module ControlRegister (
  input  in_is_branch,
  input  in_is_jump_register,
  input  in_is_jump_register_save,
  input  in_is_jump,
  input  in_set_less,
  input  in_load,
  input  in_store,
  input  [3:0] in_ALUopt,
  input  in_is_imediate,
  input  in_is_write_register,
  input  WE,
  input  clock,
  output is_branch,
  output is_junp_register,
  output is_jump_register_save,
  output is_jump,
  output set_less,
  output load,
  output store,
  output [3:0] ALUopt,
  output is_imediate,
  output is_write_register
);

  Register #(.width(13)) register_1 (
    .D({in_is_write_register, in_is_imediate, in_ALUopt, in_store, in_load, in_set_less, in_is_jump, in_is_jump_register_save, in_is_jump_register, in_is_branch}),
    .en(WE), .clk(clock),
    .Q({is_write_register, is_imediate, ALUopt, store, load, set_less, is_jump, is_jump_register_save, is_junp_register, is_branch}));  // open: clr
endmodule

module ID_EXE (
  input  [31:0] in_op,
  input  [31:0] in_A,
  input  [31:0] in_B,
  input  [4:0] in_SA,
  input  [31:0] is_next_line,
  input  [31:0] in_sw_value,
  input  clock,
  input  WE,
  output [31:0] op,
  output [31:0] A,
  output [31:0] B,
  output [4:0] SA,
  output [31:0] next_line,
  output [31:0] sw_value
);

  Register #(.width(32)) register_1 (.D(in_op), .en(WE), .clk(clock), .Q(op));  // open: clr
  Register #(.width(32)) register_2 (.D(in_A), .en(WE), .clk(clock), .Q(A));  // open: clr
  Register #(.width(32)) register_3 (.D(in_B), .en(WE), .clk(clock), .Q(B));  // open: clr
  Register #(.width(5)) register_4 (.D(in_SA), .en(WE), .clk(clock), .Q(SA));  // open: clr
  Register #(.width(32)) register_5 (.D(is_next_line), .en(WE), .clk(clock), .Q(next_line));  // open: clr
  Register #(.width(32)) register_6 (.D(in_sw_value), .en(WE), .clk(clock), .Q(sw_value));  // open: clr
endmodule

module EXE_MEM (
  input  [31:0] in_B,
  input  [31:0] in_op,
  input  [31:0] in_value,
  input  [31:0] in_next_line,
  input  [31:0] in_sw_value,
  input  WE,
  input  clock,
  output [31:0] B,
  output [31:0] op,
  output [31:0] value,
  output [31:0] next_line,
  output [31:0] sw_value
);

  Register #(.width(32)) register_1 (.D(in_B), .en(WE), .clk(clock), .Q(B));  // open: clr
  Register #(.width(32)) register_2 (.D(in_op), .en(WE), .clk(clock), .Q(op));  // open: clr
  Register #(.width(32)) register_3 (.D(in_value), .en(WE), .clk(clock), .Q(value));  // open: clr
  Register #(.width(32)) register_4 (.D(in_next_line), .en(WE), .clk(clock), .Q(next_line));  // open: clr
  Register #(.width(32)) register_5 (.D(in_sw_value), .en(WE), .clk(clock), .Q(sw_value));  // open: clr
endmodule

module MEM_WB (
  input  [31:0] in_op,
  input  [31:0] in_mem_value,
  input  [31:0] in_ALU_value,
  input  clock,
  input  WE,
  output [31:0] op,
  output [31:0] mem_value,
  output [31:0] ALU_value
);

  Register #(.width(32)) register_1 (.D(in_op), .en(WE), .clk(clock), .Q(op));  // open: clr
  Register #(.width(32)) register_2 (.D(in_mem_value), .en(WE), .clk(clock), .Q(mem_value));  // open: clr
  Register #(.width(32)) register_3 (.D(in_ALU_value), .en(WE), .clk(clock), .Q(ALU_value));  // open: clr
endmodule
