// Logisim project mips_pipeline.circ as structural Verilog: 13 circuits, main circuit main
module main (
  output out_1,
  output out_2,
  output out_3,
  output [31:0] out_4,
  output [31:0] out_5,
  output [31:0] out_6,
  output [31:0] out_7,
  output [19:0] out_8,
  output [31:0] out_9,
  output [31:0] out_10,
  output [31:0] out_11,
  output out_12,
  output [4:0] out_13,
  output [31:0] out_14,
  output [31:0] out_15,
  output [31:0] out_16,
  output [31:0] out_17,
  output [31:0] out_18,
  output [31:0] out_19,
  output [31:0] out_20,
  output [31:0] out_21,
  output [4:0] out_22,
  output [31:0] out_23,
  output [31:0] out_24,
  output [31:0] out_25,
  output [4:0] out_26,
  output [1:0] out_27,
  output [1:0] out_28,
  output [31:0] out_29,
  output [4:0] out_30,
  output [4:0] out_31
);

  wire and_1_out, and_2_out, clock_1_out, comparator_1_eq, comparator_2_eq, controlregister_1_is_branch,
       controlregister_1_is_imediate, controlregister_1_is_jump, controlregister_1_is_jump_register_save,
       controlregister_1_is_junp_register, controlregister_1_is_write_register, controlregister_1_load,
       controlregister_1_set_less, controlregister_1_store, controlregister_2_is_imediate,
       controlregister_2_is_jump_register_save, controlregister_2_is_junp_register,
       controlregister_2_is_write_register, controlregister_2_load, controlregister_2_store,
       controlregister_3_is_imediate, controlregister_3_is_jump_register_save,
       controlregister_3_is_write_register, controlregister_3_load, controlunit_1_branch,
       controlunit_1_isimediate, controlunit_1_isjump, controlunit_1_isjumpregister,
       controlunit_1_isjumpregistersave, controlunit_1_load, controlunit_1_setless, controlunit_1_store,
       controlunit_1_writeregister, exepart_1_isbranch, not_1_out, not_2_out, not_3_out, or_1_out;
  wire [3:0] controlregister_1_aluopt, controlunit_1_aluopt;
  wire [4:0] id_exe_1_sa, multiplexer_2_out, multiplexer_11_out;
  wire [31:0] a_t, B, b_t, bit_extender_1_out, exe_mem_1_sw_value, id_exe_1_next_line, id_exe_1_sw_value,
       if_id_1_next_line, ifpart_1_next_line, mem_wb_1_alu_value, mem_wb_1_mem_value, mem_wb_1_next_line,
       multiplexer_6_out, multiplexer_7_out, multiplexer_8_out, multiplexer_9_out, multiplexer_12_out,
       multiplexer_13_out, nl;

  Clock clock_1 (.out(clock_1_out));
  IFPart ifpart_1 (
    .next_line(ifpart_1_next_line), .clock(clock_1_out), .branch(exepart_1_isbranch), .in_op(out_7),
    .enable(1'b1), .jump_value(out_4), .op(out_24), .jump(controlregister_1_is_jump),
    .is_next_line(id_exe_1_next_line), .will_branch(controlregister_1_is_branch),
    .current_line_number(out_20), .is_jump_register(controlregister_1_is_junp_register));
  IF_ID if_id_1 (
    .op(out_9), .clock(clock_1_out), .WE(1'b1), .in_next_line(ifpart_1_next_line), .in_op(out_24),
    .next_line(if_id_1_next_line));
  ControlUnit controlunit_1 (
    .isJumpRegisterSave(controlunit_1_isjumpregistersave), .store(controlunit_1_store),
    .isJumpRegister(controlunit_1_isjumpregister), .load(controlunit_1_load), .isJump(controlunit_1_isjump),
    .ALUopt(controlunit_1_aluopt), .branch(controlunit_1_branch), .SetLess(controlunit_1_setless),
    .isImediate(controlunit_1_isimediate), .writeRegister(controlunit_1_writeregister), .instruction(out_9));
  or or_1 (or_1_out, controlregister_3_is_write_register, controlregister_3_is_jump_register_save);
  Multiplexer #(.width(5), .enable("false")) multiplexer_1 (
    .in0(multiplexer_2_out), .in1({5{1'b1}}), .out(out_31), .sel(controlregister_3_is_jump_register_save));
  Multiplexer #(.width(5), .enable("false")) multiplexer_2 (
    .in0(out_14[15:11]), .in1(out_14[20:16]), .out(multiplexer_2_out), .sel(controlregister_3_is_imediate));
  // RegisterFile registerfile_1: pin names not known; wires that end beside it: out_10, clock_1_out, or_1_out, out_31, out_9[25:21], out_9[20:16], a_t, b_t
  assign bit_extender_1_out = {{16{out_9[15]}}, out_9[15:0]};  // Bit_Extender bit_extender_1
  Comparator #(.width(5)) comparator_1 (.a(out_9[25:21]), .b(out_31), .eq(comparator_1_eq));  // open: gt, lt
  Comparator #(.width(5)) comparator_2 (.a(out_9[20:16]), .b(out_31), .eq(comparator_2_eq));  // open: gt, lt
  Multiplexer #(.width(32), .enable("false")) multiplexer_3 (
    .in0(B), .in1(bit_extender_1_out), .out(out_16), .sel(controlunit_1_isimediate));
  Multiplexer #(.width(32), .enable("false")) multiplexer_4 (.in0(a_t), .in1(out_10), .out(out_5), .sel(and_2_out));
  Multiplexer #(.width(32), .enable("false")) multiplexer_5 (.in0(b_t), .in1(out_10), .out(B), .sel(and_1_out));
  and and_1 (and_1_out, comparator_2_eq, or_1_out);
  and and_2 (and_2_out, or_1_out, comparator_1_eq);
  ID_EXE id_exe_1 (
    .in_op(out_9), .in_A(out_5), .in_B(out_16), .in_SA(out_9[10:6]), .is_next_line(if_id_1_next_line),
    .in_sw_value(B), .clock(clock_1_out), .WE(1'b1), .op(out_7), .A(out_4), .B(out_25), .SA(id_exe_1_sa),
    .next_line(id_exe_1_next_line), .sw_value(id_exe_1_sw_value));
  ControlRegister controlregister_1 (
    .is_jump_register_save(controlregister_1_is_jump_register_save), .is_branch(controlregister_1_is_branch),
    .WE(1'b1), .in_is_imediate(controlunit_1_isimediate), .in_store(controlunit_1_store),
    .in_set_less(controlunit_1_setless), .in_is_jump_register_save(controlunit_1_isjumpregistersave),
    .in_is_branch(controlunit_1_branch), .in_is_jump_register(controlunit_1_isjumpregister),
    .in_is_jump(controlunit_1_isjump), .in_load(controlunit_1_load), .in_ALUopt(controlunit_1_aluopt),
    .in_is_write_register(controlunit_1_writeregister), .clock(clock_1_out),
    .is_junp_register(controlregister_1_is_junp_register), .is_jump(controlregister_1_is_jump),
    .set_less(controlregister_1_set_less), .load(controlregister_1_load), .store(controlregister_1_store),
    .ALUopt(controlregister_1_aluopt), .is_imediate(controlregister_1_is_imediate),
    .is_write_register(controlregister_1_is_write_register));
  Multiplexer #(.select(2), .width(32), .enable("false")) multiplexer_6 (
    .in0(id_exe_1_sw_value), .in1(multiplexer_13_out), .in2(out_10), .in3(id_exe_1_sw_value),
    .out(multiplexer_6_out), .sel(out_28));
  Multiplexer #(.select(2), .width(32), .enable("false")) multiplexer_7 (
    .in0(out_4), .in1(multiplexer_13_out), .in2(out_10), .in3(out_4), .out(multiplexer_7_out), .sel(out_27));
  Multiplexer #(.select(2), .width(32), .enable("false")) multiplexer_8 (
    .in0(out_25), .in1(multiplexer_13_out), .in2(out_10), .in3(out_25), .out(multiplexer_8_out), .sel(out_28));
  Multiplexer #(.width(32), .enable("false")) multiplexer_9 (
    .in0(multiplexer_8_out), .in1(out_25), .out(multiplexer_9_out), .sel(controlregister_1_is_imediate));
  EXEPart exepart_1 (
    .A(multiplexer_7_out), .isBranch(exepart_1_isbranch), .B(multiplexer_9_out), .SA(id_exe_1_sa),
    .isSetLess(controlregister_1_set_less), .ALU_Op(controlregister_1_aluopt), .value(out_17));
  Multiplexer #(.width(5), .enable("false")) multiplexer_10 (
    .in0(multiplexer_11_out), .in1({5{1'b1}}), .out(out_22), .sel(controlregister_2_is_jump_register_save));
  Multiplexer #(.width(5), .enable("false")) multiplexer_11 (
    .in0(out_6[15:11]), .in1(out_6[20:16]), .out(multiplexer_11_out), .sel(controlregister_2_is_imediate));
  EXE_MEM exe_mem_1 (
    .in_op(out_7), .in_value(out_17), .in_next_line(id_exe_1_next_line), .in_sw_value(multiplexer_6_out),
    .WE(1'b1), .clock(clock_1_out), .op(out_6), .value(out_15), .next_line(nl), .sw_value(exe_mem_1_sw_value));  // open: in_B, B
  Forward forward_1 (
    .mem_is_write(controlregister_2_is_write_register), .wb_is_write(controlregister_3_is_write_register),
    .mem_in(out_22), .wb_in(out_31), .rt_in(out_7[25:21]), .rd_in(out_7[20:16]), .forwardA(out_27),
    .forwardB(out_28));
  ControlRegister controlregister_2 (
    .is_jump_register_save(controlregister_2_is_jump_register_save), .WE(1'b1),
    .in_is_imediate(controlregister_1_is_imediate), .in_store(controlregister_1_store),
    .in_is_jump_register_save(controlregister_1_is_jump_register_save),
    .in_is_jump_register(controlregister_1_is_junp_register), .in_load(controlregister_1_load),
    .in_is_write_register(controlregister_1_is_write_register), .clock(clock_1_out),
    .is_junp_register(controlregister_2_is_junp_register), .load(controlregister_2_load),
    .store(controlregister_2_store), .is_imediate(controlregister_2_is_imediate),
    .is_write_register(controlregister_2_is_write_register));  // open: is_branch, in_set_less, in_is_branch, in_is_jump, in_ALUopt, is_jump, set_less, ALUopt
  Bit_Extender #(.in_width(32), .out_width(20)) bit_extender_2 (.in(out_15), .out(out_8));
  not not_1 (not_1_out, 1'b1);
  // MIPS_RAM mips_ram_1: pin names not known; wires that end beside it: out_8, exe_mem_1_sw_value, controlregister_2_store, 4'b1111, clock_1_out, controlregister_2_load, not_1_out, out_19
  not not_2 (not_2_out, controlregister_2_load);
  not not_3 (not_3_out, controlregister_2_is_jump_register_save);
  Multiplexer #(.width(32), .enable("false")) multiplexer_12 (
    .in0(out_19), .in1(out_15), .out(multiplexer_12_out), .sel(not_2_out));
  Multiplexer #(.width(32), .enable("false")) multiplexer_13 (
    .in0(nl), .in1(multiplexer_12_out), .out(multiplexer_13_out), .sel(not_3_out));
  MEM_WB mem_wb_1 (
    .in_op(out_6), .in_mem_value(out_19), .in_ALU_value(out_15), .in_next_line(nl), .clock(clock_1_out),
    .WE(1'b1), .op(out_14), .mem_value(mem_wb_1_mem_value), .ALU_value(mem_wb_1_alu_value),
    .next_line(mem_wb_1_next_line));
  ControlRegister controlregister_3 (
    .is_jump_register_save(controlregister_3_is_jump_register_save), .WE(1'b1),
    .in_is_imediate(controlregister_2_is_imediate),
    .in_is_jump_register_save(controlregister_2_is_jump_register_save),
    .in_is_jump_register(controlregister_2_is_junp_register), .in_load(controlregister_2_load),
    .in_is_write_register(controlregister_2_is_write_register), .clock(clock_1_out),
    .load(controlregister_3_load), .is_imediate(controlregister_3_is_imediate),
    .is_write_register(controlregister_3_is_write_register));  // open: is_branch, in_store, in_set_less, in_is_branch, in_is_jump, in_ALUopt, is_junp_register, is_jump, set_less, store, ALUopt
  WBPart wbpart_1 (
    .is_jump_register(controlregister_3_is_jump_register_save), .load(controlregister_3_load),
    .ALU_value(mem_wb_1_alu_value), .Mem_value(mem_wb_1_mem_value), .next_line(mem_wb_1_next_line),
    .WriteValue(out_10));

  assign out_11 = out_7;
  assign out_13 = out_9[20:16];
  assign out_18 = out_14;
  assign out_21 = out_9;
  assign out_23 = out_4;
  assign out_26 = out_7[25:21];
  assign out_29 = out_25;
  assign out_30 = out_7[20:16];

  // Other names for the same wires on the sheet: A[31:0] = out_5

  // Notes on the sheet:
  //   op
  //   A
  //   B
  //   value
endmodule

module IFPart (
  input  enable,
  input  clock,
  input  [31:0] in_op,
  input  [31:0] jump_value,
  input  is_jump_register,
  input  [31:0] is_next_line,
  input  jump,
  input  branch,
  input  will_branch,
  output [31:0] current_line_number,
  output [31:0] op,
  output [31:0] next_line
);

  wire and_1_out;
  wire [27:0] bit_extender_2_out, shifter_1_out;
  wire [31:0] adder_1_out, bit_extender_1_out, mipsprogramrom_1_p1, multiplexer_1_out, multiplexer_2_out,
       register_1_q, shifter_2_out;

  Register #(.width(32)) register_1 (.D(current_line_number), .en(enable), .clk(clock), .Q(register_1_q));  // open: clr
  assign bit_extender_1_out = {{16{1'b0}}, in_op[15:0]};  // Bit_Extender bit_extender_1
  assign bit_extender_2_out = {{2{1'b0}}, in_op[25:0]};  // Bit_Extender bit_extender_2
  Shifter #(.width(28)) shifter_1 (.in(bit_extender_2_out), .\dist (5'b00010), .out(shifter_1_out));
  Shifter #(.width(32)) shifter_2 (.in(bit_extender_1_out), .\dist (5'b00010), .out(shifter_2_out));
  Multiplexer #(.width(32), .enable("false")) multiplexer_1 (
    .in0(register_1_q), .in1({is_next_line[31:28], shifter_1_out}), .out(multiplexer_1_out), .sel(jump));
  Adder #(.width(32)) adder_1 (.a(is_next_line), .b(shifter_2_out), .out(adder_1_out));  // open: cin, cout
  and and_1 (and_1_out, branch, will_branch);
  Multiplexer #(.width(32), .enable("false")) multiplexer_2 (
    .in0(multiplexer_1_out), .in1(adder_1_out), .out(multiplexer_2_out), .sel(and_1_out));
  // MIPSProgramROM mipsprogramrom_1: pin names not known; wires that end beside it: mipsprogramrom_1_p1, op
  Multiplexer #(.width(32), .enable("false")) multiplexer_3 (
    .in0(multiplexer_2_out), .in1(jump_value), .out(mipsprogramrom_1_p1), .sel(is_jump_register));
  Adder #(.width(32)) adder_2 (.a(mipsprogramrom_1_p1), .b(32'h4), .out(current_line_number));  // open: cin, cout

  assign next_line = current_line_number;

  // Notes on the sheet:
  //   contents of mipsprogramrom_1 (hex, n*v repeats v):
  //   addu $s1, $zero, $zero  addu $s3, $zero, $zero  addiu $sp, $sp, -4      addiu $s0, $0, 5        sw
  //   $s0, 0($sp)  jal HAILSTONE   nop     addiu $sp, $sp, 4       addu $s1, $s1, $v0      addiu $sp, $sp,
  //   -12     sw $s1, 8($sp)  addiu $s1, $s1, 1       sw $s1, 4($sp)  addiu $s1, $s1, 1       sw $s1,
  //   0($sp)  lw $s2, 8($sp)  addu $s3, $s2, $zero    lw $s2, 4($sp)  addu $s3, $s2, $s3      lw $s2,
  //   0($sp)  addu $s3, $s2, $s3      nop     nop     nop     nop     nop  HAILSTONE:         addiu $sp,
  //   $sp, -8      sw $ra, 4($sp)  sw $fp, 0($sp)  addu $fp, $sp, $zero    lw $t0, 8($fp)  addiu $t1,
  //   $zero, 1     addu $t2, $zero, $zero WHILE:   beq $t0, $t1, WHILE_OUT         nop # delayed slot
  //   WHILE_IN:    addiu $t2, $t2, 1       andi $t3, $t0, 1        bne $t3, $zero, ELSE    nop # delayed
  //   slot IF:  sra $t0, $t0, 1         j WHILE         nop ELSE:       addu $t4, $t0, $t0      addu $t0,
  //   $t0, $t4      addiu $t0, $t0, 1       j WHILE         nop WHILE_OUT:  lw $ra, 4($sp)  lw $fp, 0($sp)
  //   addiu $sp, $sp, 8       addu $v0, $t2, $zero    jr $ra  nop
endmodule

module IDPart (
  input  [31:0] write_data,
  input  clock,
  input  is_write_register,
  input  is_jump_register_save,
  input  is_imediate,
  input  [31:0] old_op,
  input  [31:0] op,
  output [31:0] A,
  output [31:0] B,
  output [4:0] SA
);

  wire [4:0] multiplexer_1_out, multiplexer_2_out;
  wire [31:0] bit_extender_1_out, registerfile_1_p8;

  Multiplexer #(.width(5), .enable("false")) multiplexer_1 (
    .in0(multiplexer_2_out), .in1({5{1'b1}}), .out(multiplexer_1_out), .sel(is_jump_register_save));
  Multiplexer #(.width(5), .enable("false")) multiplexer_2 (
    .in0(old_op[15:11]), .in1(old_op[20:16]), .out(multiplexer_2_out), .sel(is_imediate));
  // RegisterFile registerfile_1: pin names not known; wires that end beside it: write_data, clock, is_write_register, multiplexer_1_out, op[25:21], op[20:16], A, registerfile_1_p8
  assign bit_extender_1_out = {{16{op[15]}}, op[15:0]};  // Bit_Extender bit_extender_1
  Multiplexer #(.width(32), .enable("false")) multiplexer_3 (
    .in0(registerfile_1_p8), .in1(bit_extender_1_out), .out(B), .sel(is_imediate));

  assign SA = op[10:6];
endmodule

module EXEPart (
  input  [31:0] A,
  input  [31:0] B,
  input  isSetLess,
  input  [3:0] ALU_Op,
  input  [4:0] SA,
  output isBranch,
  output [31:0] value
);

  wire comparator_1_lt;
  wire [31:0] bit_extender_1_out, mips_alu_1_p7;

  Comparator #(.width(32)) comparator_1 (.a(A), .b(B), .lt(comparator_1_lt));  // open: gt, eq
  // Mips_ALU mips_alu_1: pin names not known; wires that end beside it: B, A, A, B, ALU_Op, SA, mips_alu_1_p7
  assign bit_extender_1_out = {{31{1'b0}}, comparator_1_lt};  // Bit_Extender bit_extender_1
  Multiplexer #(.width(32), .enable("false")) multiplexer_1 (
    .in0(mips_alu_1_p7), .in1(bit_extender_1_out), .out(value), .sel(isSetLess));
  Comparator #(.width(32)) comparator_2 (.a(32'h1), .b(value), .eq(isBranch));  // open: gt, lt
endmodule

module MEMPart (
  input  [31:0] op,
  input  [31:0] data,
  input  store,
  input  clock,
  input  load,
  input  clear,
  output [31:0] value
);

  wire [19:0] bit_extender_1_out;

  Bit_Extender #(.in_width(32), .out_width(20), .\type ("zero")) bit_extender_1 (.in(op), .out(bit_extender_1_out));
  // MIPS_RAM mips_ram_1: pin names not known; wires that end beside it: bit_extender_1_out, data, store, 4'b1111, clock, load, clear, value
endmodule

module WBPart (
  input  is_jump_register,
  input  load,
  input  [31:0] ALU_value,
  input  [31:0] Mem_value,
  input  [31:0] next_line,
  output [31:0] WriteValue
);

  wire [31:0] multiplexer_2_out;

  Multiplexer #(.width(32), .enable("false")) multiplexer_1 (
    .in0(multiplexer_2_out), .in1(next_line), .out(WriteValue), .sel(is_jump_register));
  Multiplexer #(.width(32), .enable("false")) multiplexer_2 (
    .in0(ALU_value), .in1(Mem_value), .out(multiplexer_2_out), .sel(load));
endmodule

module ControlUnit (
  input  [31:0] instruction,
  output branch,
  output isJumpRegister,
  output isJumpRegisterSave,
  output isJump,
  output SetLess,
  output load,
  output store,
  output [3:0] ALUopt,
  output isImediate,
  output writeRegister
);

  wire comparator_1_eq;
  wire [12:0] funcRom_data, opRom_data;

  Comparator #(.width(6)) comparator_1 (.a({6{1'b0}}), .b(instruction[31:26]), .eq(comparator_1_eq));  // open: gt, lt
  ROM #(.addrWidth(6), .dataWidth(13)) opRom (.addr(instruction[31:26]), .data(opRom_data));
  ROM #(.addrWidth(6), .dataWidth(13)) funcRom (.addr(instruction[5:0]), .data(funcRom_data));
  Multiplexer #(.width(13), .enable("false")) multiplexer_1 (
    .in0(opRom_data), .in1(funcRom_data),
    .out({writeRegister, isImediate, ALUopt, store, load, SetLess, isJump, isJumpRegisterSave, isJumpRegister, branch}),
    .sel(comparator_1_eq));

  // Notes on the sheet:
  //   contents of opRom (hex, n*v repeats v):
  //   0 0 8 100c 581 481 0 0 0 1900 1810 1810 1c00 1d00 1e00 20*0 1920 7*0 940
  //   contents of funcRom (hex, n*v repeats v):
  //   1000 0 1200 1280 4*0 a 24*0 1100 0 1300 1400 1500 1600 1700 0 0 1010 1010
endmodule

module IF_ID (
  input  [31:0] in_op,
  input  [31:0] in_next_line,
  input  WE,
  input  clock,
  output [31:0] op,
  output [31:0] next_line
);

  Register #(.width(32)) register_1 (.D(in_op), .en(WE), .clk(clock), .Q(op));  // open: clr
  Register #(.width(32)) register_2 (.D(in_next_line), .en(WE), .clk(clock), .Q(next_line));  // open: clr
endmodule

module ControlRegister (
  input  in_is_branch,
  input  in_is_jump_register,
  input  in_is_jump_register_save,
  input  in_is_jump,
  input  in_set_less,
  input  in_load,
  input  in_store,
  input  [3:0] in_ALUopt,
  input  in_is_imediate,
  input  in_is_write_register,
  input  WE,
  input  clock,
  output is_branch,
  output is_junp_register,
  output is_jump_register_save,
  output is_jump,
  output set_less,
  output load,
  output store,
  output [3:0] ALUopt,
  output is_imediate,
  output is_write_register
);

  Register #(.width(13)) register_1 (
    .D({in_is_write_register, in_is_imediate, in_ALUopt, in_store, in_load, in_set_less, in_is_jump, in_is_jump_register_save, in_is_jump_register, in_is_branch}),
    .en(WE), .clk(clock),
    .Q({is_write_register, is_imediate, ALUopt, store, load, set_less, is_jump, is_jump_register_save, is_junp_register, is_branch}));  // open: clr
endmodule

module ID_EXE (
  input  [31:0] in_op,
  input  [31:0] in_A,
  input  [31:0] in_B,
  input  [4:0] in_SA,
  input  [31:0] is_next_line,
  input  [31:0] in_sw_value,
  input  clock,
  input  WE,
  output [31:0] op,
  output [31:0] A,
  output [31:0] B,
  output [4:0] SA,
  output [31:0] next_line,
  output [31:0] sw_value
);

  Register #(.width(32)) register_1 (.D(in_op), .en(WE), .clk(clock), .Q(op));  // open: clr
  Register #(.width(32)) register_2 (.D(in_A), .en(WE), .clk(clock), .Q(A));  // open: clr
  Register #(.width(32)) register_3 (.D(in_B), .en(WE), .clk(clock), .Q(B));  // open: clr
  Register #(.width(5)) register_4 (.D(in_SA), .en(WE), .clk(clock), .Q(SA));  // open: clr
  Register #(.width(32)) register_5 (.D(is_next_line), .en(WE), .clk(clock), .Q(next_line));  // open: clr
  Register #(.width(32)) register_6 (.D(in_sw_value), .en(WE), .clk(clock), .Q(sw_value));  // open: clr
endmodule

module EXE_MEM (
  input  [31:0] in_B,
  input  [31:0] in_op,
  input  [31:0] in_value,
  input  [31:0] in_next_line,
  input  [31:0] in_sw_value,
  input  WE,
  input  clock,
  output [31:0] B,
  output [31:0] op,
  output [31:0] value,
  output [31:0] next_line,
  output [31:0] sw_value
);

  Register #(.width(32)) register_1 (.D(in_B), .en(WE), .clk(clock), .Q(B));  // open: clr
  Register #(.width(32)) register_2 (.D(in_op), .en(WE), .clk(clock), .Q(op));  // open: clr
  Register #(.width(32)) register_3 (.D(in_value), .en(WE), .clk(clock), .Q(value));  // open: clr
  Register #(.width(32)) register_4 (.D(in_next_line), .en(WE), .clk(clock), .Q(next_line));  // open: clr
  Register #(.width(32)) register_5 (.D(in_sw_value), .en(WE), .clk(clock), .Q(sw_value));  // open: clr
endmodule

module MEM_WB (
  input  [31:0] in_op,
  input  [31:0] in_mem_value,
  input  [31:0] in_ALU_value,
  input  [31:0] in_next_line,
  input  clock,
  input  WE,
  output [31:0] op,
  output [31:0] mem_value,
  output [31:0] ALU_value,
  output [31:0] next_line
);

  Register #(.width(32)) register_1 (.D(in_op), .en(WE), .clk(clock), .Q(op));  // open: clr
  Register #(.width(32)) register_2 (.D(in_mem_value), .en(WE), .clk(clock), .Q(mem_value));  // open: clr
  Register #(.width(32)) register_3 (.D(in_ALU_value), .en(WE), .clk(clock), .Q(ALU_value));  // open: clr
  Register #(.width(32)) register_4 (.D(in_next_line), .en(WE), .clk(clock), .Q(next_line));  // open: clr
endmodule

module Forward (
  input  mem_is_write,
  input  wb_is_write,
  input  [4:0] mem_in,
  input  [4:0] wb_in,
  input  [4:0] rt_in,
  input  [4:0] rd_in,
  output [1:0] forwardA,
  output [1:0] forwardB
);

  wire and_1_out, and_2_out, and_7_out, and_8_out, comparator_1_eq, comparator_1_lt, comparator_2_eq,
       comparator_3_eq, comparator_4_eq, comparator_5_eq, comparator_6_eq, not_1_out, not_2_out, xor_1_out,
       xor_2_out;
  wire [1:0] and_3_out, and_5_out, multiplexer_1_out, multiplexer_2_out;

  Comparator #(.width(5)) comparator_1 (
    .a(mem_in), .b({5{1'b0}}), .eq(comparator_1_eq), .lt(comparator_1_lt));  // open: gt
  Comparator #(.width(5)) comparator_2 (.a(wb_in), .b({5{1'b0}}), .eq(comparator_2_eq));  // open: gt, lt
  not not_1 (not_1_out, comparator_1_eq);
  not not_2 (not_2_out, comparator_2_eq);
  Comparator #(.width(5)) comparator_3 (.a(mem_in), .b(rt_in), .eq(comparator_3_eq));  // open: gt, lt
  Comparator #(.width(5)) comparator_4 (.a(rt_in), .b(wb_in), .eq(comparator_4_eq));  // open: gt, lt
  Comparator #(.width(5)) comparator_5 (.a(mem_in), .b(rd_in), .eq(comparator_5_eq));  // open: gt, lt
  Comparator #(.width(5)) comparator_6 (.a(rd_in), .b(wb_in), .eq(comparator_6_eq));  // open: gt, lt
  and and_1 (and_1_out, not_2_out, wb_is_write);
  and and_2 (and_2_out, not_1_out, mem_is_write);
  and and_3 (and_3_out[0], and_2_out, comparator_3_eq);
  and and_4 (and_3_out[1], comparator_4_eq, and_1_out);
  and and_5 (and_5_out[0], and_2_out, comparator_5_eq);
  and and_6 (and_5_out[1], comparator_6_eq, and_1_out);
  xor xor_1 (xor_1_out, and_3_out[0], and_3_out[1]);
  xor xor_2 (xor_2_out, and_5_out[0], and_5_out[1]);
  and and_7 (and_7_out, and_3_out[1], and_3_out[0]);
  and and_8 (and_8_out, and_5_out[1], and_5_out[0]);
  Multiplexer #(.width(2), .enable("false")) multiplexer_1 (
    .in0(2'b00), .in1(2'b01), .out(multiplexer_1_out), .sel(and_7_out));
  Multiplexer #(.width(2), .enable("false")) multiplexer_2 (
    .in0(2'b00), .in1(2'b10), .out(multiplexer_2_out), .sel(and_8_out));
  Multiplexer #(.width(2), .enable("false")) multiplexer_3 (
    .in0(multiplexer_1_out), .in1(and_3_out), .out(forwardA), .sel(xor_1_out));
  Multiplexer #(.width(2), .enable("false")) multiplexer_4 (
    .in0(multiplexer_2_out), .in1(and_5_out), .out(forwardB), .sel(xor_2_out));

  // Notes on the sheet:
  //   mem_in: pull=up
  //   wb_in: pull=up
endmodule
